// Logisim project conveyor.circ as structural Verilog: 5 circuits, main circuit main
module main (
  input  \Захват ,
  input  \Вкл_Выкл ,
  input  \Скорость ,
  input  ar
);

  wire CLK_out, \конвейер_1_индикатор_заполненности_лапы , \конвейер_1_индикатор_захвата ,
       \конвейер_1_индикатор_остановки_конвейера ;
  wire [1:0] \конвейер_1_position ;
  wire [3:0] \конвейер_1_belt ;
  wire [8:0] demultiplexer_1_out0, demultiplexer_1_out1, demultiplexer_1_out2, demultiplexer_1_out3;

  Clock CLK (.out(CLK_out));
  LED \u_Индикатор_захвата  (.in(\конвейер_1_индикатор_захвата ));
  \Конвейер  \u_конвейер_1  (
    .CLK(CLK_out), .\ЗАХВАТ (\Захват ), .\ВКЛ_ВЫКЛ (\Вкл_Выкл ), .\СКОРОСТЬ (\Скорость ), .ar(ar),
    .\Индикатор_захвата (\конвейер_1_индикатор_захвата ),
    .\Индикатор_остановки_конвейера (\конвейер_1_индикатор_остановки_конвейера ),
    .\Индикатор_заполненности_лапы (\конвейер_1_индикатор_заполненности_лапы ), .belt(\конвейер_1_belt ),
    .position(\конвейер_1_position ));
  LED \u_Индикатор_остановки_контейнера  (.in(\конвейер_1_индикатор_остановки_конвейера ));
  LED \u_Индикатор_захвата_2  (.in(\конвейер_1_индикатор_заполненности_лапы ));
  Demultiplexer #(.select(2), .width(9)) demultiplexer_1 (
    .out0(demultiplexer_1_out0), .out1(demultiplexer_1_out1), .out2(demultiplexer_1_out2),
    .out3(demultiplexer_1_out3), .in(9'h19e), .sel(\конвейер_1_position ));  // open: en
  DotMatrix #(.matrixcols(3), .matrixrows(3)) dotmatrix_1 (
    .col0(3'b000), .col1({1'b0, \конвейер_1_belt [2], 1'b0}), .col2(3'b000));
  DotMatrix #(.matrixcols(3), .matrixrows(3)) dotmatrix_2 (
    .col0(3'b000), .col1({1'b0, \конвейер_1_belt [3], 1'b0}), .col2(3'b000));
  DotMatrix #(.matrixcols(3), .matrixrows(3)) dotmatrix_3 (
    .col0(demultiplexer_1_out1[8:6]), .col1(demultiplexer_1_out1[5:3]), .col2(demultiplexer_1_out1[2:0]));
  DotMatrix #(.matrixcols(3), .matrixrows(3)) dotmatrix_4 (
    .col0(demultiplexer_1_out0[8:6]), .col1(demultiplexer_1_out0[5:3]), .col2(demultiplexer_1_out0[2:0]));
  DotMatrix #(.matrixcols(3), .matrixrows(3)) dotmatrix_5 (
    .col0(3'b000), .col1({1'b0, \конвейер_1_belt [1], 1'b0}), .col2(3'b000));
  DotMatrix #(.matrixcols(3), .matrixrows(3)) dotmatrix_6 (
    .col0(3'b000), .col1({1'b0, \конвейер_1_belt [0], 1'b0}), .col2(3'b000));
  DotMatrix #(.matrixcols(3), .matrixrows(3)) dotmatrix_7 (
    .col0(demultiplexer_1_out2[8:6]), .col1(demultiplexer_1_out2[5:3]), .col2(demultiplexer_1_out2[2:0]));
  DotMatrix #(.matrixcols(3), .matrixrows(3)) dotmatrix_8 (
    .col0(demultiplexer_1_out3[8:6]), .col1(demultiplexer_1_out3[5:3]), .col2(demultiplexer_1_out3[2:0]));
endmodule

module \Лента  (
  input  CLK,
  input  _3AXBAT,
  input  \АВТО_ЛАПА ,
  input  [1:0] \Положение_лапы ,
  input  ar,
  output \Остановка_конвейера ,
  output [3:0] belt,
  output \Изделие_на_захват 
);

  wire and_1_out, and_2_out, and_3_out, and_4_out, and_5_out, and_6_out, and_7_out, and_8_out, and_9_out,
       and_10_out, and_11_out, and_12_out, demultiplexer_1_out0, demultiplexer_1_out1, demultiplexer_1_out2,
       demultiplexer_1_out3, or_2_out, or_3_out, or_4_out, or_5_out, s_r_ff_1_qn, s_r_ff_2_qn, s_r_ff_3_qn;

  or or_1 (\Остановка_конвейера , _3AXBAT, \АВТО_ЛАПА );
  Demultiplexer #(.select(2)) demultiplexer_1 (
    .out0(demultiplexer_1_out0), .out1(demultiplexer_1_out1), .out2(demultiplexer_1_out2),
    .out3(demultiplexer_1_out3), .in(1'b1), .sel(\Положение_лапы ));  // open: en
  and and_1 (and_1_out, ~\Остановка_конвейера , belt[0]);  // AND_Gate
  and and_2 (and_2_out, ~belt[0], ~\Остановка_конвейера );  // AND_Gate
  or or_2 (or_2_out, and_2_out, and_3_out);
  and and_3 (and_3_out, _3AXBAT, demultiplexer_1_out0);
  and and_4 (and_4_out, ~\Остановка_конвейера , belt[3]);  // AND_Gate
  S_R_Flip_Flop s_r_ff_1 (
    .S(and_1_out), .clk(CLK), .R(or_2_out), .Q(belt[3]), .Qn(s_r_ff_1_qn), .preset(ar));  // open: reset, en
  and and_5 (and_5_out, s_r_ff_1_qn, ~\Остановка_конвейера );  // AND_Gate
  and and_6 (and_6_out, _3AXBAT, demultiplexer_1_out1);
  S_R_Flip_Flop s_r_ff_2 (
    .S(and_4_out), .clk(CLK), .R(or_3_out), .Q(belt[2]), .Qn(s_r_ff_2_qn), .preset(ar));  // open: reset, en
  or or_3 (or_3_out, and_5_out, and_6_out);
  and and_7 (and_7_out, ~\Остановка_конвейера , belt[2]);  // AND_Gate
  and and_8 (and_8_out, s_r_ff_2_qn, ~\Остановка_конвейера );  // AND_Gate
  or or_4 (or_4_out, and_8_out, and_9_out);
  and and_9 (and_9_out, _3AXBAT, demultiplexer_1_out2);
  S_R_Flip_Flop s_r_ff_3 (
    .S(and_7_out), .clk(CLK), .R(or_4_out), .Q(belt[1]), .Qn(s_r_ff_3_qn), .preset(ar));  // open: reset, en
  and and_10 (and_10_out, ~\Остановка_конвейера , belt[1]);  // AND_Gate
  and and_11 (and_11_out, s_r_ff_3_qn, ~\Остановка_конвейера );  // AND_Gate
  or or_5 (or_5_out, and_11_out, and_12_out);
  and and_12 (and_12_out, _3AXBAT, demultiplexer_1_out3);
  S_R_Flip_Flop s_r_ff_4 (.S(and_10_out), .clk(CLK), .R(or_5_out), .Q(belt[0]), .preset(ar));  // open: Qn, reset, en
  Multiplexer #(.select(2)) multiplexer_1 (
    .in0(belt[3]), .in1(belt[2]), .in2(belt[1]), .in3(belt[0]), .out(\Изделие_на_захват ),
    .sel(\Положение_лапы ));  // open: en
endmodule

module \Лапа  (
  input  CLK,
  input  \Изделие ,
  input  _3AXBAT,
  input  \Вкл_Выкл ,
  input  \Скорость ,
  input  ar,
  output \АВТО ,
  output \Заполнение ,
  output [1:0] Position
);

  wire and_1_out, and_2_out, and_3_out, and_4_out, and_5_out, and_6_out, not_1_out, or_1_out, or_2_out;

  S_R_Flip_Flop s_r_ff_1 (.S(_3AXBAT), .clk(CLK), .R(and_6_out), .Q(\АВТО ), .reset(ar));  // open: Qn, preset, en
  not not_1 (not_1_out, \Вкл_Выкл );
  or or_1 (or_1_out, \АВТО , not_1_out);
  and and_1 (and_1_out, \АВТО , ~and_6_out);  // AND_Gate
  and and_2 (and_2_out, ~\АВТО , \Скорость );  // AND_Gate
  and and_3 (and_3_out, or_1_out, and_4_out);
  or or_2 (or_2_out, and_1_out, and_2_out);
  and and_4 (and_4_out, or_2_out, ~_3AXBAT);  // AND_Gate
  and and_5 (and_5_out, \Изделие , _3AXBAT);
  Counter #(.width(2), .max('h3)) counter_1 (
    .load(and_3_out), .count(and_4_out), .Q(Position), .clk(CLK));  // open: D, carry, clr
  S_R_Flip_Flop s_r_ff_2 (
    .S(and_5_out), .clk(CLK), .R(and_6_out), .Q(\Заполнение ), .reset(ar));  // open: Qn, preset, en
  and and_6 (and_6_out, \АВТО , ~Position[0], ~Position[1]);  // AND_Gate
endmodule

module \Захват  (
  input  \ЗАХВАТ ,
  input  \АВТО ,
  output \Индикатор_захвата 
);

  wire and_1_out;

  and and_1 (and_1_out, \ЗАХВАТ , ~\АВТО );  // AND_Gate
  S_R_Flip_Flop #(.trigger("high")) s_r_ff_1 (
    .S(and_1_out), .clk(1'b1), .R(\АВТО ), .Q(\Индикатор_захвата ));  // open: Qn, preset, reset, en
endmodule

module \Конвейер  (
  input  CLK,
  input  \ЗАХВАТ ,
  input  \ВКЛ_ВЫКЛ ,
  input  \СКОРОСТЬ ,
  input  ar,
  output \Индикатор_захвата ,
  output \Индикатор_остановки_конвейера ,
  output \Индикатор_заполненности_лапы ,
  output [3:0] belt,
  output [1:0] position
);

  wire \лапа_1_авто , \лента_1_изделие_на_захват ;

  \Захват  \u_захват_1  (.\ЗАХВАТ (\ЗАХВАТ ), .\АВТО (\лапа_1_авто ), .\Индикатор_захвата (\Индикатор_захвата ));
  \Лапа  \u_лапа_1  (
    ._3AXBAT(\Индикатор_захвата ), .\Вкл_Выкл (\ВКЛ_ВЫКЛ ), .\Скорость (\СКОРОСТЬ ), .CLK(CLK),
    .\Изделие (\лента_1_изделие_на_захват ), .ar(ar), .\АВТО (\лапа_1_авто ),
    .\Заполнение (\Индикатор_заполненности_лапы ), .Position(position));
  \Лента  \u_лента_1  (
    ._3AXBAT(\Индикатор_захвата ), .\АВТО_ЛАПА (\лапа_1_авто ), .\Положение_лапы (position), .CLK(CLK),
    .ar(ar), .\Остановка_конвейера (\Индикатор_остановки_конвейера ), .belt(belt),
    .\Изделие_на_захват (\лента_1_изделие_на_захват ));
endmodule
